// Logisim project SelectionSort.circ as structural Verilog: 4 circuits, main circuit main
module main (
  input  done,
  input  in_2,
  input  [7:0] data,
  input  data_av
);

  wire clk_out, not_1_out, rst_out, undriven_3;
  wire [7:0] controlled_buffer_1_out, ram_1_data, undriven, undriven_2;

  Clock clk (.out(clk_out));
  Button rst (.out(rst_out));
  Selection_Sort selection_sort_1 ();  // open: data_in, data, address, data_out
  not not_1 (not_1_out, undriven_3);
  RAM ram_1 (.addr(undriven), .data(ram_1_data), .sel(in_2), .clk(clk_out), .ld(undriven_3));  // open: clr
  assign controlled_buffer_1_out = not_1_out ? undriven_2 : 8'bz;  // Controlled_Buffer controlled_buffer_1

  // Notes on the sheet:
  //   data_in
  //   data_out
endmodule

module Selection_Sort (
  input  [7:0] data_in,
  input  [7:0] address,
  input  [7:0] data,
  input  [7:0] data_out
);
endmodule

module DataPath (
  input  selData_out,
  input  wrAux,
  input  selMuxAux,
  input  [7:0] data_in,
  input  wrMin,
  input  selMin,
  input  selAddr1,
  input  wrOrder,
  input  selAddr0,
  input  wrI,
  input  seli1,
  input  selInc,
  input  wrStartAddr,
  input  [7:0] data,
  input  selComp,
  input  wrJ,
  input  wrSize,
  input  reset,
  input  clock,
  output [7:0] data_out,
  output aux_t_min,
  output [7:0] address,
  output i_dt_min,
  output lt_size
);

  wire comparator_1_gt, comparator_1_lt, comparator_2_eq;
  wire [6:0] subtractor_1_out;
  wire [7:0] adder_1_out, and_1_out, multiplexer_1_out, multiplexer_2_out, multiplexer_3_out,
       multiplexer_4_out, multiplexer_6_out, multiplexer_7_out, reg_aux_q, reg_i_q, reg_J_q, reg_min_q,
       reg_order_q, reg_size_q, reg_startAddr_q, xor_1_out;

  // Probe on data
  Register reg_order (.D(data), .en(wrOrder), .Q(reg_order_q), .clk(clock), .clr(reset));
  Register reg_startAddr (.D(data), .en(wrStartAddr), .Q(reg_startAddr_q), .clk(clock), .clr(reset));
  Register reg_size (.D(data), .en(wrSize), .Q(reg_size_q), .clk(clock), .clr(reset));
  assign and_1_out = 8'h1 & reg_order_q;  // AND_Gate and_1, 8 bits wide
  // Probe on data_in
  Multiplexer #(.width(8), .disabled(0), .enable("false")) multiplexer_1 (
    .in0(adder_1_out), .in1(reg_startAddr_q), .out(multiplexer_1_out), .sel(seli1));
  Register reg_i (.D(multiplexer_1_out), .en(wrI), .Q(reg_i_q), .clk(clock), .clr(reset));
  Register reg_J (.D(adder_1_out), .en(wrJ), .Q(reg_J_q), .clk(clock), .clr(reset));
  Multiplexer #(.width(8), .enable("false")) multiplexer_2 (
    .in0(xor_1_out), .in1(data_in), .out(multiplexer_2_out), .sel(selMuxAux));
  // Probe on reg_aux_q
  Register reg_aux (.D(multiplexer_2_out), .en(wrAux), .Q(reg_aux_q), .clk(clock), .clr(reset));
  Multiplexer #(.width(8), .enable("false")) multiplexer_3 (
    .in0(reg_i_q), .in1(reg_J_q), .out(multiplexer_3_out), .sel(selMin));
  Multiplexer #(.width(8), .disabled(0), .enable("false")) multiplexer_4 (
    .in0(reg_i_q), .in1(reg_J_q), .out(multiplexer_4_out), .sel(selInc));
  Register reg_min (.D(multiplexer_3_out), .en(wrMin), .Q(reg_min_q), .clk(clock), .clr(reset));
  Adder adder_1 (.a(multiplexer_4_out), .b(8'h1), .out(adder_1_out));  // open: cin, cout
  assign xor_1_out = data_in ^ reg_aux_q;  // XOR_Gate xor_1, 8 bits wide
  Comparator comparator_1 (.a(reg_aux_q), .b(data_in), .gt(comparator_1_gt), .lt(comparator_1_lt));  // open: eq
  Multiplexer #(.enable("false")) multiplexer_5 (
    .in0(comparator_1_gt), .in1(comparator_1_lt), .out(aux_t_min), .sel(and_1_out[0]));
  Multiplexer #(.width(8), .enable("false")) multiplexer_6 (
    .in0(reg_J_q), .in1(reg_i_q), .out(multiplexer_6_out), .sel(selAddr0));
  not not_1 (i_dt_min, comparator_2_eq);
  Comparator comparator_2 (.a(reg_min_q), .b(reg_i_q), .eq(comparator_2_eq));  // open: gt, lt
  // Probe on multiplexer_7_out
  Multiplexer #(.width(8), .disabled(0), .enable("false")) multiplexer_7 (
    .in0(adder_1_out), .in1(reg_J_q), .out(multiplexer_7_out), .sel(selComp));
  Multiplexer #(.width(8), .disabled(0), .enable("false")) multiplexer_8 (
    .in0(xor_1_out), .in1(reg_aux_q), .out(data_out), .sel(selData_out));
  Multiplexer #(.width(8), .enable("false")) multiplexer_9 (
    .in0(reg_min_q), .in1(multiplexer_6_out), .out(address), .sel(selAddr1));
  Subtractor subtractor_1 (
    .a(multiplexer_7_out), .b(reg_size_q), .out({lt_size, subtractor_1_out}));  // open: bin, bout
  // Probe on data_out

  // Other names for the same wires on the sheet: clk = clock; rst = reset

  // Notes on the sheet:
  //   5   6
  //   ld StartAddr
  //   i++
  //   xor
  //   data_in
  //   || i++
  //   j++
  //   i
  //   j
  //   i++
  //   j++
  //   aux
  //   mem[min]
  //   order == 0 >
  //   order == 1 <
  //   i + 1 < size
  //   j < size
  //   xor
  //   aux
  //   j
  //   i
  //   min
endmodule

module Control_Path (
  input  in_1,
  input  in_2,
  output [3:0] out_3
);

  wire [3:0] undriven;

  Register #(.width(4)) register_1 (.D(undriven), .Q(out_3), .clk(in_1), .clr(in_2));  // open: en

  // Other names for the same wires on the sheet: clk = in_1; rst = in_2
endmodule
